# Fritzing sketch Circuit-BreadBoard (saved by Fritzing 0.9.2b)
circuit board: 8.46667cm x 5.64444cm
breadboards: 1

parts:
  TA7291P = TA7291P [package=HSIP10-P-2.54(THT)]
  Raspberry_Pi_Zero1 = Raspberry Pi Zero
  Lipo_Battery = LIPO-1000mAh [package=lipo-1000]
  R1 = Resistor [tolerance=±5% resistance=10k package=THT]
  R2 = Resistor [tolerance=±5% resistance=3.0 package=THT]
  Motor1 = DC Motor
  Zero_Lipo = mystery part, 6 pins [chip_label="Zero Lipo"]
  C1 = Electrolytic Capacitor [package="100 mil [THT, electrolytic]"]
  R3 = Resistor [tolerance=±5% resistance=1k package=THT]
  LED1 = LED - 3mm [color="White (4500K)" package="3 mm [THT]"]
  LED2 = LED - 3mm [color="White (4500K)" package="3 mm [THT]"]

nets:
  GND: TA7291P.GND, Raspberry_Pi_Zero1.GND, Lipo_Battery.-, Zero_Lipo.pin2, Zero_Lipo.pin5, C1.-, LED1.cathode, LED2.cathode
  N1: TA7291P.OUT1, Motor1.pin_1
  N2: TA7291P.Vref, R1.Pin_0
  N3: TA7291P.IN1, Raspberry_Pi_Zero1.GIPO18
  N4: TA7291P.IN2, Raspberry_Pi_Zero1.GIPO19
  VCC: TA7291P.Vcc, Raspberry_Pi_Zero1.5V, Zero_Lipo.pin1
  N5: TA7291P.Vs, R1.Pin_1, R2.Pin_0
  N6: TA7291P.OUT2, Motor1.pin_2
  N7: Raspberry_Pi_Zero1.GIPO4, Zero_Lipo.pin3
  N8: Raspberry_Pi_Zero1.GIPO12, R3.Pin_0
  N9: Lipo_Battery.+, R2.Pin_1, Zero_Lipo.pin6, C1.+
  N10: R3.Pin_1, LED1.anode, LED2.anode

notes:
  電源バスライン
  上方(YZピン)： 5.0V Zero LiPo 出力
  下方(WXピン)： 3.7V LiPo Battery

custom parts:
  TA7291P: The IC are Full-Bridge Driver. 4 modes available (CW / CCW / STOP / BRAKE) and PWM control. Output current:1.0 A (AVE.) 2.0 A (PEAK)
  Electrolytic Capacitor: A small electrolytic capacitor
